// Logisim project control-logic.circ as structural Verilog: 1 circuit, main circuit control_logic
module control_logic (
  input  [31:0] Instruction,
  input  BrEq,
  input  BrLt,
  output PCSel,
  output RegWEn,
  output [2:0] ImmSel,
  output BrUn,
  output ASel,
  output BSel,
  output [3:0] ALUSel,
  output MemWEn,
  output [1:0] WBSel
);

  wire and_1_out, and_2_out, comparator_1_eq, comparator_2_eq, comparator_3_eq, comparator_4_eq,
       comparator_5_eq, comparator_6_eq, comparator_7_eq, comparator_8_eq, comparator_9_eq, comparator_10_eq,
       comparator_11_eq, comparator_12_eq, comparator_13_eq, comparator_14_eq, comparator_15_eq,
       comparator_17_eq, comparator_18_eq, not_1_out, or_1_out, or_3_out, or_4_out;
  wire [3:0] multiplexer_1_out, multiplexer_3_out;

  Comparator #(.width(7)) comparator_1 (.a(Instruction[6:0]), .b(7'b0110011), .eq(comparator_1_eq));  // open: gt, lt
  Comparator #(.width(7)) comparator_2 (.a(Instruction[6:0]), .b(7'b0010011), .eq(comparator_2_eq));  // open: gt, lt
  Comparator #(.width(7)) comparator_3 (.a(Instruction[6:0]), .b(7'b0000011), .eq(comparator_3_eq));  // open: gt, lt
  Comparator #(.width(7)) comparator_4 (.a(Instruction[6:0]), .b(7'b1101111), .eq(comparator_4_eq));  // open: gt, lt
  Comparator #(.width(7)) comparator_5 (.a(Instruction[6:0]), .b(7'b1100111), .eq(comparator_5_eq));  // open: gt, lt
  Comparator #(.width(7)) comparator_6 (.a(Instruction[6:0]), .b(7'b0010011), .eq(comparator_6_eq));  // open: gt, lt
  Comparator #(.width(7)) comparator_7 (.a(Instruction[6:0]), .b(7'b1100111), .eq(comparator_7_eq));  // open: gt, lt
  Comparator #(.width(7)) comparator_8 (.a(Instruction[6:0]), .b(7'b0000011), .eq(comparator_8_eq));  // open: gt, lt
  Comparator #(.width(7)) comparator_9 (.a(Instruction[6:0]), .b(7'b0100011), .eq(comparator_9_eq));  // open: gt, lt
  Comparator #(.width(7)) comparator_10 (.a(Instruction[6:0]), .b(7'b1100011), .eq(comparator_10_eq));  // open: gt, lt
  Comparator #(.width(7)) comparator_11 (.a(Instruction[6:0]), .b(7'b0010111), .eq(comparator_11_eq));  // open: gt, lt
  Comparator #(.width(7)) comparator_12 (.a(Instruction[6:0]), .b(7'b0110111), .eq(comparator_12_eq));  // open: gt, lt
  Comparator #(.width(7)) comparator_13 (.a(Instruction[6:0]), .b(7'b1101111), .eq(comparator_13_eq));  // open: gt, lt
  not not_1 (not_1_out, or_3_out);
  or or_1 (or_1_out, comparator_11_eq, comparator_12_eq);
  or or_2 (RegWEn, comparator_1_eq, comparator_2_eq, comparator_3_eq, comparator_4_eq, comparator_5_eq);
  Comparator #(.width(3)) comparator_14 (.a(Instruction[14:12]), .b(3'b001), .eq(comparator_14_eq));  // open: gt, lt
  Comparator #(.width(3)) comparator_15 (.a(Instruction[14:12]), .b(3'b101), .eq(comparator_15_eq));  // open: gt, lt
  or or_3 (or_3_out, comparator_15_eq, comparator_14_eq);
  and and_1 (and_1_out, or_3_out, comparator_6_eq);
  and and_2 (and_2_out, not_1_out, comparator_6_eq);
  or or_4 (or_4_out, and_2_out, comparator_7_eq, comparator_8_eq);
  Priority_Encoder priority_encoder_1 (
    .in0(and_1_out), .in1(or_4_out), .in2(comparator_9_eq), .in3(comparator_10_eq), .in4(or_1_out),
    .in5(comparator_13_eq), .out(ImmSel));  // open: in6, in7, en_in, gs, en_out
  Comparator #(.width(7)) comparator_16 (.a(Instruction[6:0]), .b(7'b0110011), .eq(BSel));  // open: gt, lt
  Comparator #(.width(7)) comparator_17 (
    .a(Instruction[31:25]), .b(7'b0100000), .eq(comparator_17_eq));  // open: gt, lt
  Comparator #(.width(3)) comparator_18 (.a(Instruction[14:12]), .b(3'b000), .eq(comparator_18_eq));  // open: gt, lt
  Comparator #(.width(3)) comparator_19 (.a(Instruction[14:12]), .b(3'b101));  // open: gt, eq, lt
  Comparator #(.width(3)) comparator_20 (.b(3'b101));  // open: a, gt, eq, lt
  Multiplexer #(.width(4)) multiplexer_1 (.in0(4'b0000), .out(multiplexer_1_out), .sel(comparator_17_eq));  // open: in1
  Multiplexer #(.width(4)) multiplexer_2 (
    .in0(multiplexer_1_out), .in1(multiplexer_3_out), .sel(comparator_18_eq));  // open: out
  Multiplexer #(.width(4)) multiplexer_3 (
    .in0(4'b1101), .in1(4'b0101), .out(multiplexer_3_out), .sel(comparator_17_eq));

  // Other names for the same wires on the sheet: opcode[6:0] = Instruction[6:0]; funct3[2:0] = Instruction[14:12];
  //   funct7[6:0] = Instruction[31:25]

  // Notes on the sheet:
  //   INPUTS to your circuit
  //   DON'T CHANGE THE LOCATIONS OF THE INPUTS AND OUTPUTS!
  //   OUTPUT from your circuit
endmodule
